# Fritzing sketch AutoDoorOpener (saved by Fritzing 0.9.2b)
breadboards: 1

parts:
  PIC_16F877A1 = PIC 16F877A [package=THT]
  Power_plug1 = Power plug
  C1 = Ceramic Capacitor [capacitance=100nF package="100 mil [THT, multilayer]"]
  U1 = LCD-16X2 [package=lcd-16x2_noholes]
  R18 = Resistor [tolerance=±5% resistance=5k package=THT]
  Q1 = NPN-Transistor [package="TO92 [THT]"]
  R19 = Resistor [tolerance=±5% resistance=220 package=THT]
  Power_plug2 = Power plug
  Power_plug3 = Power plug
  Q6 = MOSFET-NCHANNEL [package=to220v]
  Q7 = MOSFET-NCHANNEL [package=to220v]
  Q8 = MOSFET-NCHANNEL [package=to220v]
  Q9 = MOSFET-NCHANNEL [package=to220v]
  Q10 = MOSFET-NCHANNEL [package=to220v]
  Q11 = MOSFET-NCHANNEL [package=to220v]
  R20 = Resistor [tolerance=±5% resistance=220 package=THT]
  R21 = Resistor [tolerance=±5% resistance=220 package=THT]
  R22 = Resistor [tolerance=±5% resistance=220 package=THT]
  R23 = Resistor [tolerance=±5% resistance=220 package=THT]
  R24 = Resistor [tolerance=±5% resistance=220 package=THT]
  R25 = Resistor [tolerance=±5% resistance=220 package=THT]
  L1 = Solenoid
  L2 = Solenoid
  L3 = Solenoid
  L4 = Solenoid
  L5 = Solenoid
  L6 = Solenoid
  U5 = L298 [package=multiwatt15]
  M2 = DC Motor
  Encoder = Rotary Encoder [package=THT]
  Q12 = NPN-Transistor [package="TO92 [THT]"]
  R28 = Resistor [tolerance=±5% resistance=220 package=THT]
  Q13 = NPN-Transistor [package="TO92 [THT]"]
  R29 = Resistor [tolerance=±5% resistance=220 package=THT]
  R30 = Resistor [tolerance=±5% resistance=220 package=THT]
  S5 = Pushbutton [package=THT]
  S6 = Pushbutton [package=THT]
  S7 = Pushbutton [package=THT]
  S8 = Pushbutton [package=THT]
  S9 = Pushbutton [package=THT]
  S10 = Pushbutton [package=THT]
  S11 = Pushbutton [package=THT]
  S12 = Pushbutton [package=THT]
  S13 = Pushbutton [package=THT]
  S14 = Pushbutton [package=THT]
  S15 = Pushbutton [package=THT]
  S16 = Pushbutton [package=THT]
  S17 = Pushbutton [package=THT]
  S18 = Pushbutton [package=THT]
  S19 = Pushbutton [package=THT]
  S20 = Pushbutton [package=THT]

nets:
  N1: PIC_16F877A1.MCLR, R30.Pin_0
  N2: PIC_16F877A1.RA0/AN0, S10.leg0, S11.leg0, S12.leg0, S18.leg0
  N3: PIC_16F877A1.RA1/AN1, S6.leg0, S7.leg0, S8.leg0, S20.leg0
  N4: PIC_16F877A1.RA2/AN2, S9.leg0, S14.leg0, S15.leg0, S16.leg0
  N5: PIC_16F877A1.RA3/AN3, S5.leg0, S13.leg0, S17.leg0, S19.leg0
  N6: PIC_16F877A1.RA4, Q6.G, Q7.G, Q8.G, Q9.G, Q10.G, Q11.G
  N7: PIC_16F877A1.RE0/RD/AN5, U1.RS
  N8: PIC_16F877A1.RE1/WR/AN6, U1.R_W
  N9: PIC_16F877A1.RE2/CS/AN7, U1.E
  VCC: PIC_16F877A1.VDD#10, Power_plug1.VCC, C1.1, U1.VDD, Power_plug3.VCC, R20.Pin_0, R21.Pin_1, R22.Pin_0, R23.Pin_0, R24.Pin_1, R25.Pin_1, Encoder.EncoderPinA, R30.Pin_1
  GND: PIC_16F877A1.VSS#11, Power_plug1.GND, C1.0, U1.VSS, R18.Pin_1, Power_plug3.GND, Encoder.EncoderPinB
  N10: PIC_16F877A1.RC2, Encoder.EncoderPinC
  N11: PIC_16F877A1.RD0/PSP0, U1.DB0
  N12: PIC_16F877A1.RD1/PSP1, U1.DB1
  N13: PIC_16F877A1.RD2/PSP2, U1.DB2
  N14: PIC_16F877A1.RD3/PSP3, U1.DB3
  N15: PIC_16F877A1.RC5, U5.ENA
  N16: PIC_16F877A1.RC6/TX/CK, U5.IN2
  N17: PIC_16F877A1.RC7/RX/DT, U5.IN1
  N18: PIC_16F877A1.RD4/PSP4, U1.DB4
  N19: PIC_16F877A1.RD5/PSP5, U1.DB5
  N20: PIC_16F877A1.RD6/PSP6, U1.DB6
  N21: PIC_16F877A1.RD7/PSP7, U1.DB7
  N22: PIC_16F877A1.VSS#30, Q1.E, Power_plug2.GND, Q12.E, Q13.E
  N23: PIC_16F877A1.VDD#31, U1.A, Power_plug2.VCC, U5.VLS
  N24: PIC_16F877A1.RB0/INT, Q1.C
  N25: PIC_16F877A1.RB1, Q12.C
  N26: PIC_16F877A1.RB2, Q13.C
  N27: PIC_16F877A1.RB4, S8.leg1, S12.leg1, S13.leg1, S14.leg1
  N28: PIC_16F877A1.RB5, S7.leg1, S11.leg1, S15.leg1, S19.leg1
  N29: PIC_16F877A1.RB6, S6.leg1, S10.leg1, S16.leg1, S17.leg1
  N30: PIC_16F877A1.RB7, S5.leg1, S9.leg1, S18.leg1, S20.leg1
  N31: U1.VO, R18.Pin_0
  N32: U1.K, U5.GND
  N33: Q1.B, R19.Pin_0
  N34: Q6.D, R21.Pin_0
  N35: Q6.S, L1.pin1
  N36: Q7.D, R24.Pin_0
  N37: Q7.S, L3.pin1
  N38: Q8.D, R25.Pin_0
  N39: Q8.S, L5.pin1
  N40: Q9.D, R20.Pin_1
  N41: Q9.S, L2.pin1
  N42: Q10.D, R22.Pin_1
  N43: Q10.S, L4.pin1
  N44: Q11.D, R23.Pin_1
  N45: Q11.S, L6.pin1
  N46: U5.OUT1, M2.pin_1
  N47: U5.OUT2, M2.pin_2
  N48: Q12.B, R28.Pin_0
  N49: Q13.B, R29.Pin_0
