# Fritzing sketch AutomaticDoorOpener (saved by Fritzing 0.8.7b)
breadboards: 1

parts:
  Power_plug1 = Power plug  # not connected
  D1 = Rectifier Diode [part_number=1N4001 package="300 mil [THT]"]
  D2 = Rectifier Diode [part_number=1N4001 package="300 mil [THT]"]
  D3 = Rectifier Diode [part_number=1N4001 package="300 mil [THT]"]
  D4 = Rectifier Diode [part_number=1N4001 package="300 mil [THT]"]
  C1 = Electrolytic Capacitor [capacitance=1µF package="100 mil [THT, electrolytic]"]

nets:
  N1: D1.cathode, D2.cathode, C1.-
  N2: D1.anode, D4.cathode
  N3: D2.anode, D3.cathode
  N4: D3.anode, D4.anode, C1.+
