# Fritzing sketch CarPassword (saved by Fritzing 0.8.7b)
circuit board: 7.69cm x 9.42125cm

parts:
  VCC1 = Battery
  R1 = Resistor [tolerance=±5% resistance=1.5 package=THT]
  R2 = Resistor [tolerance=±5% resistance=1 package=THT]
  C1 = Electrolytic Capacitor [capacitance=4.7mF package="100 mil [THT, electrolytic]"]
  D1 = Diode [package=diode-1n4001]
  PIC_16F877A1 = PIC 16F877A [package=THT]
  R4 = Resistor [tolerance=±5% resistance=4.7k package=THT]  # not connected
  XTAL1 = Crystal [frequency="16 Mhz" package=THT]
  S1 = Pushbutton [package=THT]
  S2 = Pushbutton [package=THT]
  S3 = Pushbutton [package=THT]
  S4 = Pushbutton [package=THT]
  S5 = Pushbutton [package=THT]
  S6 = Pushbutton [package=THT]
  S7 = Pushbutton [package=THT]
  S8 = Pushbutton [package=THT]
  S9 = Pushbutton [package=THT]
  S10 = Pushbutton [package=THT]
  R5 = Resistor [tolerance=±5% resistance=10k package=THT]
  S11 = Pushbutton [package=THT]
  S12 = Pushbutton [package=THT]
  S13 = Pushbutton [package=THT]
  S14 = Pushbutton [package=THT]
  S15 = Pushbutton [package=THT]
  S16 = Pushbutton [package=THT]
  S17 = Pushbutton [package=THT]
  S18 = Pushbutton [package=THT]
  S19 = Pushbutton [package=THT]
  S20 = Pushbutton [package=THT]
  S21 = Pushbutton [package=THT]
  S22 = Pushbutton [package=THT]
  Q1 = MOSFET-NCHANNEL [package=to220v]
  Q2 = Basic FET P-Channel [package="TO220 [THT]"]
  S23 = Pushbutton [package=THT]
  S24 = Pushbutton [package=THT]
  S25 = Pushbutton [package=THT]
  S26 = Pushbutton [package=THT]
  S27 = Pushbutton [package=THT]
  S28 = Pushbutton [package=THT]
  R6 = Resistor [tolerance=±5% resistance=5k package=THT]

nets:
  N1: VCC1.-, C1.-, PIC_16F877A1.RC6/TX/CK, S11.leg0, R6.Pin_0
  N2: VCC1.+, D1.A
  N3: R1.Pin_0, C1.+, D1.C
  N4: R1.Pin_1, R2.Pin_0, PIC_16F877A1.RC7/RX/DT, S9.leg0
  N5: PIC_16F877A1.RA5/AN4/SS, R5.Pin_1
  N6: PIC_16F877A1.RE2/CS/AN7, Q1.G, Q2.gate
  N7: PIC_16F877A1.VDD#10, S22.leg0
  N8: PIC_16F877A1.VSS#11, S21.leg0
  N9: PIC_16F877A1.OSC1/CLKIN, S17.leg0
  N10: PIC_16F877A1.OSC2/CLKOUT, S20.leg0
  N11: PIC_16F877A1.RC0, XTAL1.pin_1
  N12: PIC_16F877A1.RC1, XTAL1.pin_0
  N13: PIC_16F877A1.RC2, S19.leg0
  N14: PIC_16F877A1.RC3, S16.leg0
  N15: PIC_16F877A1.RD0/PSP0, S10.leg0
  N16: PIC_16F877A1.RD1/PSP1, S15.leg0
  N17: PIC_16F877A1.RD2/PSP2, S13.leg0
  N18: PIC_16F877A1.RD3/PSP3, S14.leg0
  N19: PIC_16F877A1.RC4, S12.leg0
  N20: PIC_16F877A1.RC5, S18.leg0
  N21: PIC_16F877A1.RD4/PSP4, S1.leg0
  N22: PIC_16F877A1.RD5/PSP5, S2.leg0
  N23: PIC_16F877A1.RD6/PSP6, S8.leg0
  N24: PIC_16F877A1.RD7/PSP7, S3.leg0
  N25: PIC_16F877A1.VSS#30, S4.leg0
  N26: PIC_16F877A1.VDD#31, S5.leg0
  N27: PIC_16F877A1.RB0/INT, S6.leg0
  N28: PIC_16F877A1.RB1, S7.leg0
  N29: R5.Pin_0, S27.leg0
  N30: Q1.D, S25.leg0
  N31: Q1.S, S26.leg0
  N32: Q2.drain, S23.leg0
  N33: Q2.source, S24.leg0
  N34: S28.leg0, R6.Pin_1
