# Fritzing sketch CarPassword2 (saved by Fritzing 0.8.7b)
breadboards: 1

parts:
  PIC_16F877A1 = PIC 16F877A [package=THT]
  LCD1 = LCD screen
  VCC1 = 4 x AAA Battery Mount
  R2 = Resistor [tolerance=±5% resistance=5k package=THT]
  R3 = Resistor [tolerance=±5% resistance=10k package=THT]
  XTAL1 = Crystal [frequency="4 MHz" package=THT]
  C1 = Ceramic Capacitor [capacitance=0.1nF package="100 mil [THT, multilayer]"]
  C2 = Ceramic Capacitor [capacitance=0.1nF package="100 mil [THT, multilayer]"]
  C3 = Ceramic Capacitor [capacitance=100nF package="100 mil [THT, multilayer]"]
  Q1 = MOSFET-NCHANNEL [package=to220v]
  Q2 = Basic FET P-Channel [package="DPak [SMD]"]
  C4 = Ceramic Capacitor [capacitance=100nF package="100 mil [THT, multilayer]"]

nets:
  N1: PIC_16F877A1.MCLR, R3.Pin_0
  N2: PIC_16F877A1.RA2/AN2, Q1.G, Q2.Gate
  N3: PIC_16F877A1.RA3/AN3, LCD1.V0, LCD1.RS, R2.Pin_0
  N4: PIC_16F877A1.RA4, LCD1.R/W
  N5: PIC_16F877A1.RA5/AN4/SS, LCD1.E
  VDD: PIC_16F877A1.VDD, LCD1.VDD, LCD1.LED+, VCC1.+, R3.Pin_1, C3.1, C4.0
  VSS: PIC_16F877A1.VSS, LCD1.VSS, LCD1.LED-, VCC1.-, R2.Pin_1, C1.0, C2.1, C3.0, C4.1
  N6: PIC_16F877A1.OSC1/CLKIN, XTAL1.pin_0, C1.1
  N7: PIC_16F877A1.OSC2/CLKOUT, XTAL1.pin_1, C2.0
  N8: PIC_16F877A1.RC0, LCD1.DB0
  N9: PIC_16F877A1.RC1, LCD1.DB1
  N10: PIC_16F877A1.RC2, LCD1.DB2
  N11: PIC_16F877A1.RC3, LCD1.DB3
  N12: PIC_16F877A1.RC4, LCD1.DB4
  N13: PIC_16F877A1.RC5, LCD1.DB5
  N14: PIC_16F877A1.RC6/TX/CK, LCD1.DB6
  N15: PIC_16F877A1.RC7/RX/DT, LCD1.DB7
