# Fritzing sketch CarPassword_Complete (saved by Fritzing 0.8.7b)
breadboards: 1

parts:
  LCD2 = LCD screen
  PIC_16F877A2 = PIC 16F877A [package=THT]
  S17 = Pushbutton [package=THT]
  S18 = Pushbutton [package=THT]
  S19 = Pushbutton [package=THT]
  S20 = Pushbutton [package=THT]
  S21 = Pushbutton [package=THT]
  S22 = Pushbutton [package=THT]
  S23 = Pushbutton [package=THT]
  S24 = Pushbutton [package=THT]
  S25 = Pushbutton [package=THT]
  S26 = Pushbutton [package=THT]
  S27 = Pushbutton [package=THT]
  S28 = Pushbutton [package=THT]
  S29 = Pushbutton [package=THT]
  S30 = Pushbutton [package=THT]
  S31 = Pushbutton [package=THT]
  S32 = Pushbutton [package=THT]
  Q1 = NPN-Transistor [package="TO92 [THT]"]
  R1 = Resistor [tolerance=±5% resistance=330 package=THT]
  XTAL2 = Crystal [frequency="4 MHz" package=THT]
  C3 = Ceramic Capacitor [capacitance=27pF package="100 mil [THT, multilayer]"]
  C4 = Ceramic Capacitor [capacitance=27pF package="100 mil [THT, multilayer]"]
  Q2 = NPN-Transistor [package="TO92 [THT]"]
  R2 = Resistor [tolerance=±5% resistance=220 package=THT]
  Dr_alrm_actv = LED - 5mm [color="Blue (525nm)" package="5 mm [THT]"]
  LCD_err = LED - 5mm [color="Red (633nm)" package="5 mm [THT]"]
  R3 = Resistor [tolerance=±5% resistance=330 package=THT]
  R4 = Resistor [tolerance=±5% resistance=330 package=THT]
  LED1 = LED - 5mm [color="Green (565nm)" package="5 mm [THT]"]
  R5 = Resistor [tolerance=±5% resistance=220 package=THT]
  U1 = Voltage Regulator - 5V [package="TO220 [THT]"]
  V1 = DC Power [voltage=12V]
  C5 = Tantalum Capacitor [capacitance=10µF package="100 mil [THT, tantalum]"]
  C6 = Electrolytic Capacitor [capacitance=10µF package="100 mil [THT, electrolytic]"]
  C8 = Electrolytic Capacitor [capacitance=0.1µF package="100 mil [THT, electrolytic]"]
  C7 = Tantalum Capacitor [capacitance=4.7mF package="200 mil [THT, tantalum]"]
  J1 = Screw terminal - 2 pins [package=THT]
  SPKR1 = Loudspeaker
  Q3 = Basic FET N-Channel [package="TO220 [THT]"]
  Q4 = PNP-Transistor [package="TO92 [THT]"]
  R6 = Resistor [tolerance=±5% resistance=10k package=THT]
  R7 = Resistor [tolerance=±5% resistance=330 package=THT]
  Q5 = NPN-Transistor [package="TO92 [THT]"]
  R8 = Resistor [tolerance=±5% resistance=330 package=THT]
  R9 = Resistor [tolerance=±5% resistance=10k package=THT]
  C9 = Tantalum Capacitor [capacitance=1μF package="100 mil [THT, tantalum]"]
  U2 = Voltage Regulator - 5V [package="TO220 [THT]"]
  R10 = Resistor [tolerance=±5% resistance=220 package=THT]
  S33 = Pushbutton [package="[THT]"]
  R11 = Resistor [tolerance=±5% resistance=10k package=THT]
  R12 = Resistor [tolerance=±5% resistance=10k package=THT]
  R13 = Resistor [tolerance=±5% resistance=10k package=THT]
  R14 = Resistor [tolerance=±5% resistance=10k package=THT]

nets:
  N1: LCD2.VSS, Q1.C
  5V: LCD2.VDD, LCD2.LED+, PIC_16F877A2.VDD, U1.output_voltage, C6.+, C8.+, C7.+, J1.pin1, R10.Pin_0, R11.Pin_0, R12.Pin_0, R13.Pin_0, R14.Pin_0
  N2: LCD2.RS, PIC_16F877A2.RC1
  N3: LCD2.R/W, PIC_16F877A2.RC2
  N4: LCD2.E, PIC_16F877A2.RC3
  N5: LCD2.DB4, PIC_16F877A2.RC4
  N6: LCD2.DB5, PIC_16F877A2.RC5
  N7: LCD2.DB6, PIC_16F877A2.RC6/TX/CK
  N8: LCD2.DB7, PIC_16F877A2.RC7/RX/DT
  N9: LCD2.LED-, Q2.C
  N10: PIC_16F877A2.MCLR, R10.Pin_1, S33.Pin_3, S33.Pin_4
  N11: PIC_16F877A2.RA2/AN2, R1.Pin_1
  N12: PIC_16F877A2.RA3/AN3, Dr_alrm_actv.anode
  N13: PIC_16F877A2.RA5/AN4/SS, LCD_err.anode
  N14: PIC_16F877A2.RE1/WR/AN6, LED1.anode
  N15: PIC_16F877A2.RE2/CS/AN7, R8.Pin_1
  GRD: PIC_16F877A2.VSS
  N16: PIC_16F877A2.OSC1/CLKIN, XTAL2.pin_1, C3.1
  N17: PIC_16F877A2.OSC2/CLKOUT, XTAL2.pin_0, C4.1
  N18: PIC_16F877A2.RC0, R2.Pin_1
  N19: PIC_16F877A2.RD0/PSP0, S17.leg0
  N20: PIC_16F877A2.RD1/PSP1, S18.leg0
  N21: PIC_16F877A2.RD2/PSP2, S19.leg0
  N22: PIC_16F877A2.RD3/PSP3, S20.leg0
  N23: PIC_16F877A2.RD4/PSP4, S17.leg1, S18.leg1, S19.leg1, S20.leg1, R14.Pin_1
  N24: PIC_16F877A2.RD5/PSP5, S21.leg1, S22.leg1, S23.leg1, S24.leg1, R11.Pin_1
  N25: PIC_16F877A2.RD6/PSP6, S25.leg1, S26.leg1, S27.leg1, S28.leg1, R12.Pin_1
  N26: PIC_16F877A2.RD7/PSP7, S29.leg1, S30.leg1, S31.leg1, S32.leg1, R13.Pin_1
  GND: Q1.E, C3.0, C4.0, Q2.E, R3.Pin_0, R4.Pin_1, R5.Pin_1, U1.GND, V1.V-, C5.-, C6.-, C8.-, C7.-, J1.pin2, Q3.source, R6.Pin_1, Q5.E, C9.-, U2.GND, S33.Pin_1
  N27: Q1.B, R1.Pin_0
  N28: Q2.B, R2.Pin_0
  N29: Dr_alrm_actv.cathode, R3.Pin_1
  N30: LCD_err.cathode, R4.Pin_0
  N31: LED1.cathode, R5.Pin_0
  12V: U1.input_voltage, C5.+, Q4.E, R9.Pin_1, U2.output_voltage
  Battery: V1.V+, C9.+, U2.input_voltage
  Battary: SPKR1.pin1
  N32: SPKR1.pin2, Q3.drain
  N33: Q3.gate, Q4.C, R6.Pin_0
  N34: Q4.B, R7.Pin_0
  N35: R7.Pin_1, Q5.C, R9.Pin_0
  N36: Q5.B, R8.Pin_0
