# Fritzing sketch CarPassword_Schematic (saved by Fritzing 0.8.7b)
breadboards: 1

parts:
  PIC_16F877A1 = PIC 16F877A [package=THT]
  LCD1 = LCD screen
  S1 = Pushbutton [package=THT]
  S2 = Pushbutton [package=THT]
  S3 = Pushbutton [package=THT]
  S4 = Pushbutton [package=THT]
  S5 = Pushbutton [package=THT]
  S6 = Pushbutton [package=THT]
  S7 = Pushbutton [package=THT]
  S8 = Pushbutton [package=THT]
  S9 = Pushbutton [package=THT]
  S10 = Pushbutton [package=THT]
  S11 = Pushbutton [package=THT]
  S12 = Pushbutton [package=THT]
  S13 = Pushbutton [package=THT]
  S14 = Pushbutton [package=THT]
  S15 = Pushbutton [package=THT]
  S16 = Pushbutton [package=THT]
  XTAL1 = Crystal [frequency="4 MHz" package=THT]
  C1 = Ceramic Capacitor [capacitance=27pF package="100 mil [THT, multilayer]"]
  C2 = Ceramic Capacitor [capacitance=27pF package="100 mil [THT, multilayer]"]
  R1 = Resistor [tolerance=±5% resistance=10k package=THT]
  S18 = Pushbutton [package=THT]
  S19 = Pushbutton [package=THT]
  Power_plug1 = Power plug
  R2 = Resistor [tolerance=±5% resistance=30 package=THT]
  R3 = Resistor [tolerance=±5% resistance=20 package=THT]
  R4 = Resistor [tolerance=±5% resistance=5k package=THT]
  Q1 = MOSFET-NCHANNEL [package=to220v]
  Q2 = Basic FET P-Channel [package="DPak [SMD]"]
  S21 = Pushbutton [package=THT]
  R5 = Resistor [tolerance=±5% resistance=10k package=THT]
  R6 = Resistor [tolerance=±5% resistance=51k package=THT]
  Q3 = NPN-Transistor [package="TO92 [THT]"]
  Q4 = NPN-Transistor [package="TO92 [THT]"]
  LED1 = LED - 5mm [color="Green (565nm)" package="5 mm [THT]"]
  R7 = Resistor [tolerance=±5% resistance=470 package=THT]
  SPKR1 = Loudspeaker
  Q5 = NPN-Transistor [package="TO92 [THT]"]
  R8 = Resistor [tolerance=±5% resistance=220 package=THT]
  R9 = Resistor [tolerance=±5% resistance=1k package=THT]
  M1 = DC Motor
  J1 = Piezo Speaker
  U2 = SN74LS32N [package="DIP14 [THT]"]
  Q6 = Basic FET P-Channel [package="TO220 [THT]"]
  LED2 = LED - 5mm [color="Red (633nm)" package="5 mm [THT]"]
  R10 = Resistor [tolerance=±5% resistance=470 package=THT]
  LED3 = LED - 5mm [color="Blue (505nm)" package="5 mm [THT]"]
  R11 = Resistor [tolerance=±5% resistance=470 package=THT]

nets:
  N1: PIC_16F877A1.MCLR, R1.Pin_1
  N2: PIC_16F877A1.RA2/AN2, Q6.gate
  N3: PIC_16F877A1.RA3/AN3, LED3.anode
  N4: PIC_16F877A1.RA5/AN4/SS, LED2.anode
  N5: PIC_16F877A1.RE0/RD/AN5, Q2.Gate
  N6: PIC_16F877A1.RE1/WR/AN6, Q1.G, Q2.source, LED1.anode
  N7: PIC_16F877A1.RE2/CS/AN7, R8.Pin_0
  VDD: PIC_16F877A1.VDD, R1.Pin_0, R2.Pin_1, R3.Pin_0, Q2.drain, U2.Vcc, Q6.drain
  VSS: PIC_16F877A1.VSS, LCD1.VSS, LCD1.LED-, C1.0, C2.0, S18.leg1, S19.leg1, Power_plug1.GND, R3.Pin_1, R4.Pin_0, R5.Pin_1, Q3.E, Q4.E, R7.Pin_1, SPKR1.pin2, Q5.E, M1.pin_2, J1.pin2, U2.GND, R10.Pin_1, R11.Pin_1
  N8: PIC_16F877A1.OSC1/CLKIN, XTAL1.pin_1, C1.1
  N9: PIC_16F877A1.OSC2/CLKOUT, XTAL1.pin_0, C2.1
  N10: PIC_16F877A1.RC0, LCD1.LED+
  N11: PIC_16F877A1.RC1, LCD1.RS
  N12: PIC_16F877A1.RC2, LCD1.R/W
  N13: PIC_16F877A1.RC3, LCD1.E
  N14: PIC_16F877A1.RD0/PSP0, S4.leg0, S8.leg0, S12.leg0, S16.leg0
  N15: PIC_16F877A1.RD1/PSP1, S1.leg0, S7.leg0, S11.leg0, S15.leg0
  N16: PIC_16F877A1.RD2/PSP2, S2.leg0, S6.leg0, S10.leg0, S14.leg0
  N17: PIC_16F877A1.RD3/PSP3, S3.leg0, S5.leg0, S9.leg0, S13.leg0
  N18: PIC_16F877A1.RC4, LCD1.DB4
  N19: PIC_16F877A1.RC5, LCD1.DB5
  N20: PIC_16F877A1.RC6/TX/CK, LCD1.DB6
  N21: PIC_16F877A1.RC7/RX/DT, LCD1.DB7
  N22: PIC_16F877A1.RD4/PSP4, S13.leg1, S14.leg1, S15.leg1, S16.leg1, U2.4B
  N23: PIC_16F877A1.RD5/PSP5, S9.leg1, S10.leg1, S11.leg1, S12.leg1, U2.4A
  N24: PIC_16F877A1.RD6/PSP6, S5.leg1, S6.leg1, S7.leg1, S8.leg1, U2.3B
  N25: PIC_16F877A1.RD7/PSP7, S1.leg1, S2.leg1, S3.leg1, S4.leg1, U2.3A
  N26: PIC_16F877A1.RB0/INT, Q4.C
  N27: PIC_16F877A1.RB4, Q3.C
  N28: PIC_16F877A1.RB5, S19.leg0
  N29: PIC_16F877A1.RB6, S18.leg0
  N30: LCD1.VDD, Q6.source
  N31: LCD1.V0, R4.Pin_1
  N32: Power_plug1.VCC, R2.Pin_0, S21.leg1, R9.Pin_1
  N33: Q1.D, S21.leg0, R6.Pin_0
  N34: Q1.S, M1.pin_1
  N35: R5.Pin_0, R6.Pin_1, Q3.B
  N36: LED1.cathode, R7.Pin_0
  N37: SPKR1.pin1, Q5.C, R9.Pin_0
  N38: Q5.B, R8.Pin_1
  N39: J1.pin1, U2.3Y, U2.4Y
  N40: LED2.cathode, R10.Pin_0
  N41: LED3.cathode, R11.Pin_0
