# Fritzing sketch CarProject_v1 (saved by Fritzing 0.8.7b)
breadboards: 1

parts:
  LCD2 = LCD screen
  PIC_16F877A2 = PIC 16F877A [package=THT]
  S17 = Pushbutton [package=THT]
  S18 = Pushbutton [package=THT]
  S19 = Pushbutton [package=THT]
  S20 = Pushbutton [package=THT]
  S21 = Pushbutton [package=THT]
  S22 = Pushbutton [package=THT]
  S23 = Pushbutton [package=THT]
  S24 = Pushbutton [package=THT]
  S25 = Pushbutton [package=THT]
  S26 = Pushbutton [package=THT]
  S27 = Pushbutton [package=THT]
  S28 = Pushbutton [package=THT]
  S29 = Pushbutton [package=THT]
  S30 = Pushbutton [package=THT]
  S31 = Pushbutton [package=THT]
  S32 = Pushbutton [package=THT]
  Q1 = NPN-Transistor [package="TO92 [THT]"]
  R1_/_13mA/0_5W = Resistor [tolerance=±5% resistance=330 package=THT]
  XTAL2 = Crystal [frequency="4 MHz" package=THT]
  C3 = Ceramic Capacitor [capacitance=27pF package="100 mil [THT, multilayer]"]
  C4 = Ceramic Capacitor [capacitance=27pF package="100 mil [THT, multilayer]"]
  Q2 = NPN-Transistor [package="TO92 [THT]"]
  R2_/_13mA_/_0_5_W = Resistor [tolerance=±5% resistance=330 package=THT]
  Dr_alrm_actv = LED - 5mm [color="Blue (525nm)" package="5 mm [THT]"]
  LCD_err = LED - 5mm [color="Red (633nm)" package="5 mm [THT]"]
  R3/10mA = Resistor [tolerance=±5% resistance=330 package=THT]
  R4 = Resistor [tolerance=±5% resistance=330 package=THT]
  LED1 = LED - 5mm [color="Green (565nm)" package="5 mm [THT]"]
  R5 = Resistor [tolerance=±5% resistance=220 package=THT]
  U1 = Voltage Regulator - 5V [package="TO220 [THT]"]
  V1 = DC Power [voltage=12V]
  C5 = Tantalum Capacitor [capacitance=10µF package="100 mil [THT, tantalum]"]
  C6 = Electrolytic Capacitor [capacitance=10µF package="100 mil [THT, electrolytic]"]
  C8 = Electrolytic Capacitor [capacitance=0.1µF package="100 mil [THT, electrolytic]"]
  C7 = Tantalum Capacitor [capacitance=4.7mF package="200 mil [THT, tantalum]"]
  J1 = Screw terminal - 2 pins [package=THT]
  SPKR1 = Loudspeaker
  Q3 = Basic FET N-Channel [package="TO220 [THT]"]
  C9 = Tantalum Capacitor [capacitance=1μF package="100 mil [THT, tantalum]"]
  U2 = Voltage Regulator - 5V [package="TO220 [THT]"]
  R10 = Resistor [tolerance=±5% resistance=10k package=THT]
  R11 = Resistor [tolerance=±5% resistance=10k package=THT]
  R12 = Resistor [tolerance=±5% resistance=10k package=THT]
  R13 = Resistor [tolerance=±5% resistance=10k package=THT]
  R14 = Resistor [tolerance=±5% resistance=10k package=THT]
  Q6 = NPN-Transistor [package="TO92 [THT]"]
  R15 = Resistor [tolerance=±5% resistance=330 package=THT]
  J2 = Piezo Speaker [part_number="Buzzer for keypad"]
  S35 = Pushbutton [package=THT]
  U3 = TLP621 [package=THT]
  J3 = Screw terminal - 2 pins [package=THT]
  R16 = Resistor [tolerance=±5% resistance=820 package=THT]
  D1 = Rectifier Diode [part_number=1N4001 package="300 mil [THT]"]
  LED2 = LED - 5mm [color="Red (633nm)" package="5 mm [THT]"]
  C10 = Ceramic Capacitor [capacitance=0.1µF package="100 mil [THT, multilayer]"]
  M1 = DC Motor [part_number="feul pump"]
  R20 = Resistor [tolerance=±5% resistance=10k package=THT]
  Q8 = Basic FET N-Channel [package="TO220 [THT]"]
  R21 = Resistor [tolerance=±5% resistance=10k package=THT]
  R22 = Resistor [tolerance=±5% resistance=15k package=THT]
  R23 = Resistor [tolerance=±5% resistance=10k package=THT]
  J5 = Screw terminal - 2 pins [package=THT]
  Q9 = NPN-Transistor [package="TO92 [THT]"]
  R24 = Resistor [tolerance=±5% resistance=330 package=THT]
  Q10 = Basic FET N-Channel [package="TO220 [THT]"]
  L1 = Inductor [part_number="Mobina Coil" package="400 mil [THT]"]
  R25 = Resistor [tolerance=±5% resistance=10k package=THT]
  R26 = Resistor [tolerance=±5% resistance=4.7k package=THT]
  U4 = RELAY [part_number="25 A max" package=relay-jzc]
  Q11 = NPN-Transistor [package="TO92 [THT]"]
  D2 = Rectifier Diode [part_number=1N4001 package="300 mil [THT]"]
  R27 = Resistor [tolerance=±5% resistance=330 package=THT]
  J6 = Screw terminal - 2 pins [package=THT]
  J7 = Screw terminal - 2 pins [part_number="hood switch" package=THT]
  J8 = Screw terminal - 2 pins [part_number="door switch" package=THT]

nets:
  N1: LCD2.VSS, Q1.C
  5V: LCD2.VDD, LCD2.LED+, PIC_16F877A2.VDD, U1.output_voltage, C6.+, C8.+, C7.+, J1.pin1, R10.Pin_0, R11.Pin_0, R12.Pin_0, R13.Pin_0, R14.Pin_0, J2.pin1, R26.Pin_1, U4.COIL1, D2.cathode
  N2: LCD2.V0, R26.Pin_0
  N3: LCD2.RS, PIC_16F877A2.RC1
  N4: LCD2.R/W, PIC_16F877A2.RC2
  N5: LCD2.E, PIC_16F877A2.RC3
  N6: LCD2.DB4, PIC_16F877A2.RC4
  N7: LCD2.DB5, PIC_16F877A2.RC5
  N8: LCD2.DB6, PIC_16F877A2.RC6/TX/CK
  N9: LCD2.DB7, PIC_16F877A2.RC7/RX/DT
  N10: LCD2.LED-, Q2.C
  N11: PIC_16F877A2.MCLR, R10.Pin_1, S35.leg1
  N12: PIC_16F877A2.RA2/AN2, R1_/_13mA/0_5W.Pin_1
  N13: PIC_16F877A2.RA3/AN3, Dr_alrm_actv.anode
  N14: PIC_16F877A2.RA5/AN4/SS, LCD_err.anode
  N15: PIC_16F877A2.RE0/RD/AN5, R15.Pin_0
  N16: PIC_16F877A2.RE1/WR/AN6, LED1.anode
  N17: PIC_16F877A2.RE2/CS/AN7, Q3.gate, R20.Pin_0
  GRD: PIC_16F877A2.VSS
  N18: PIC_16F877A2.OSC1/CLKIN, XTAL2.pin_1, C3.1
  N19: PIC_16F877A2.OSC2/CLKOUT, XTAL2.pin_0, C4.1
  N20: PIC_16F877A2.RC0, R2_/_13mA_/_0_5_W.Pin_1
  N21: PIC_16F877A2.RD0/PSP0, S17.leg0, S21.leg0, S25.leg0, S29.leg0
  N22: PIC_16F877A2.RD1/PSP1, S18.leg0, S22.leg0, S26.leg0, S32.leg0
  N23: PIC_16F877A2.RD2/PSP2, S19.leg0, S23.leg0, S27.leg0, S31.leg0
  N24: PIC_16F877A2.RD3/PSP3, S20.leg0, S24.leg0, S28.leg0, S30.leg0
  N25: PIC_16F877A2.RD4/PSP4, S17.leg1, S18.leg1, S19.leg1, S20.leg1, R14.Pin_1
  N26: PIC_16F877A2.RD5/PSP5, S21.leg1, S22.leg1, S23.leg1, S24.leg1, R11.Pin_1
  N27: PIC_16F877A2.RD6/PSP6, S25.leg1, S26.leg1, S27.leg1, S28.leg1, R12.Pin_1
  N28: PIC_16F877A2.RD7/PSP7, S29.leg1, S30.leg1, S31.leg1, S32.leg1, R13.Pin_1
  N29: PIC_16F877A2.RB0/INT, Q9.C
  N30: PIC_16F877A2.RB1, U3.Pin_4
  N31: PIC_16F877A2.RB5, J8.pin2
  N32: PIC_16F877A2.RB6, J7.pin2
  GND: Q1.E, C3.0, C4.0, Q2.E, R3/10mA.Pin_0, R4.Pin_1, R5.Pin_1, U1.GND, V1.V-, C5.-, C6.-, C8.-, C7.-, J1.pin2, Q3.source, C9.-, U2.GND, Q6.E, S35.leg0, U3.Pin_3, C10.0, R20.Pin_1, Q8.source, R21.Pin_1, R23.Pin_1, Q9.E, Q10.source, R25.Pin_1, Q11.E, J7.pin1, J8.pin1
  N33: Q1.B, R1_/_13mA/0_5W.Pin_0
  N34: Q2.B, R2_/_13mA_/_0_5_W.Pin_0
  N35: Dr_alrm_actv.cathode, R3/10mA.Pin_1
  N36: LCD_err.cathode, R4.Pin_0
  N37: LED1.cathode, R5.Pin_0
  12V: U1.input_voltage, C5.+, U2.output_voltage, C10.1, M1.pin_1, L1.pin_0, U4.MAIN, J6.pin1
  Battery: V1.V+, C9.+, U2.input_voltage
  Battary: SPKR1.pin1
  N38: SPKR1.pin2, Q3.drain
  N39: Q6.B, R15.Pin_1
  N40: Q6.C, J2.pin2
  N41: U3.Pin_1, D1.cathode, LED2.anode
  N42: U3.Pin_2, J3.pin2, LED2.cathode
  N43: J3.pin1, R16.Pin_0
  N44: R16.Pin_1, D1.anode
  N45: M1.pin_2, Q8.drain
  A1: Q8.gate, R21.Pin_0
  N46: R22.Pin_0, J5.pin2
  N47: R22.Pin_1, R23.Pin_0, R24.Pin_1
  N48: Q9.B, R24.Pin_0
  A0: Q10.gate, R25.Pin_0
  N49: Q10.drain, L1.pin_1
  N50: U4.COIL2, Q11.C, D2.anode
  To key power: U4.NO, J6.pin2
  N51: Q11.B, R27.Pin_0
  A4: R27.Pin_1

notes:
  Car Security System ,  security system for car using password , v1.1
  From Alarm System
  Sarien Output
  input from key
  power MOSFET
  70 mA
  10mA
