# Fritzing sketch TurnOnInterrupt (saved by Fritzing 0.8.7b)
breadboards: 1

parts:
  Q1 = MOSFET-NCHANNEL [package=to220v]
  Power_plug1 = Power plug
  PIC_16F877A1 = PIC 16F877A [package=THT]
  R1 = Resistor [tolerance=±5% resistance=30k package=THT]
  R2 = Resistor [tolerance=±5% resistance=10k package=THT]
  Q2 = NPN-Transistor [package="TO92 [THT]"]
  M1 = DC Motor

nets:
  N1: Q1.G, PIC_16F877A1.RA1/AN1
  N2: Q1.D, Power_plug1.VCC, R1.Pin_0
  N3: Q1.S, M1.pin_1
  N4: Power_plug1.GND, R2.Pin_1, Q2.E
  N5: PIC_16F877A1.RB4, Q2.C
  N6: R1.Pin_1, R2.Pin_0
